// Logisim project hw1_problem_14.circ as structural Verilog
module problem_14 (
  input  a,
  input  b,
  input  c,
  input  d,
  output x
);

  wire and_1_out, and_2_out, and_3_out, and_4_out, or_1_out, or_2_out;

  or or_1 (or_1_out, b, a);
  or or_2 (or_2_out, c, d);
  and and_1 (and_1_out, c, d);
  and and_2 (and_2_out, a, b);
  and and_3 (and_3_out, and_2_out, or_2_out);
  and and_4 (and_4_out, or_1_out, and_1_out);
  or or_3 (x, and_3_out, and_4_out);
endmodule
