// Logisim project Hw2_3bit_counter.circ as structural Verilog: 3 circuits, main circuit main
module main (
  input  X,
  output C,
  output A,
  output B
);

  wire and_1_out, and_2_out, clock_1_out;

  Clock clock_1 (.out(clock_1_out));
  J_K_Flip_Flop u_C (.J(and_1_out), .clk(clock_1_out), .K(and_2_out), .Q(C));  // open: Qn, preset, en, reset
  J_K_Flip_Flop u_A (.J(B), .clk(clock_1_out), .K(and_1_out), .Q(A));  // open: Qn, preset, en, reset
  J_K_Flip_Flop u_B (.J(X), .clk(clock_1_out), .K(B), .Q(B));  // open: Qn, preset, en, reset
  and and_1 (and_1_out, B, A);
  and and_2 (and_2_out, and_1_out, C);
endmodule

module hw2_prob_14 (
  input  X,
  output C,
  output A,
  output B
);

  wire and_1_out, and_2_out, clock_1_out;

  Clock clock_1 (.out(clock_1_out));
  J_K_Flip_Flop u_C (.J(and_2_out), .clk(clock_1_out), .K(and_1_out), .Q(C));  // open: Qn, preset, en, reset
  and and_1 (and_1_out, C, and_2_out);
  J_K_Flip_Flop u_A (.J(B), .clk(clock_1_out), .K(and_2_out), .Q(A));  // open: Qn, preset, en, reset
  J_K_Flip_Flop u_B (.J(X), .clk(clock_1_out), .K(B), .Q(B));  // open: Qn, preset, en, reset
  and and_2 (and_2_out, A, B);
endmodule

module Cusom_Flip_Flop (
  input  X,
  input  Y,
  output Z
);

  wire A_q, and_1_out, and_2_out, and_3_out, clock_1_out, not_1_out, or_1_out, or_2_out;

  not not_1 (not_1_out, X);
  and and_1 (and_1_out, X, A_q);
  and and_2 (and_2_out, not_1_out, Y);
  and and_3 (and_3_out, X, Z);
  D_Flip_Flop A (.clk(clock_1_out), .D(or_1_out), .Q(A_q));  // open: Qn, preset, en, reset
  or or_1 (or_1_out, and_1_out, and_2_out);
  Clock clock_1 (.out(clock_1_out));
  D_Flip_Flop B (.clk(clock_1_out), .D(or_2_out), .Q(Z));  // open: Qn, preset, en, reset
  or or_2 (or_2_out, and_1_out, and_3_out);
endmodule
