// Logisim project hw2_flip_flop.circ as structural Verilog: 1 circuit, main circuit main
module main (
  input  X,
  input  Y,
  output Z
);

  wire A_q, and_1_out, and_2_out, and_3_out, clock_1_out, not_1_out, or_1_out, or_2_out;

  not not_1 (not_1_out, X);
  and and_1 (and_1_out, X, A_q);
  and and_2 (and_2_out, not_1_out, Y);
  and and_3 (and_3_out, X, Z);
  D_Flip_Flop A (.clk(clock_1_out), .D(or_1_out), .Q(A_q));  // open: Qn, preset, en, reset
  or or_1 (or_1_out, and_1_out, and_2_out);
  Clock clock_1 (.out(clock_1_out));
  D_Flip_Flop B (.clk(clock_1_out), .D(or_2_out), .Q(Z));  // open: Qn, preset, en, reset
  or or_2 (or_2_out, and_1_out, and_3_out);
endmodule
