// Logisim project hw2_full_adder.circ as structural Verilog: 1 circuit, main circuit main
module main (
  input  c,
  input  x,
  input  y,
  output Sum,
  output carry_out
);

  wire and_1_out, and_2_out, and_3_out, and_4_out, and_5_out, and_6_out, and_7_out, and_8_out, and_9_out,
       and_10_out, not_1_out, not_2_out, not_3_out, not_4_out, or_2_out;

  and and_1 (and_1_out, y, x);
  and and_2 (and_2_out, x, x);
  and and_3 (and_3_out, y, y);
  or or_1 (carry_out, and_1_out, and_6_out);
  not not_1 (not_1_out, and_2_out);
  not not_2 (not_2_out, and_3_out);
  and and_4 (and_4_out, x, not_2_out);
  or or_2 (or_2_out, and_4_out, and_5_out);
  and and_5 (and_5_out, not_1_out, y);
  and and_6 (and_6_out, or_2_out, c);
  not not_3 (not_3_out, and_7_out);
  and and_7 (and_7_out, c, c);
  not not_4 (not_4_out, and_8_out);
  and and_8 (and_8_out, or_2_out, or_2_out);
  and and_9 (and_9_out, c, not_4_out);
  and and_10 (and_10_out, not_3_out, or_2_out);
  or or_3 (Sum, and_9_out, and_10_out);
endmodule
